// Logisim project RISC16_Saje.circ as structural Verilog: 5 circuits, main circuit main
module main (
);

  wire clock_1_out;
  wire [3:0] rom_1_data, rom_1_data_2;
  wire [7:0] rom_1_data_3;
  wire [15:0] pc_1_o;

  Clock clock_1 (.out(clock_1_out));
  PC pc_1 (.EN(clock_1_out), .CLK(clock_1_out), .O(pc_1_o));  // open: JMP_ADDR, JMP_EN
  ROM #(.addrWidth(16), .dataWidth(16)) rom_1 (.addr(pc_1_o), .data({rom_1_data_3, rom_1_data_2, rom_1_data}));
endmodule

module OneTickLatch (
  input  CLK,
  output out_2
);

  wire not_1_out, register_1_q;

  Register #(.width(1)) register_1 (.D(1'b1), .clk(CLK), .Q(register_1_q));  // open: en, clr
  not not_1 (not_1_out, register_1_q);
  and and_1 (out_2, not_1_out, CLK);
endmodule

module PC (
  input  [15:0] JMP_ADDR,
  input  JMP_EN,
  input  EN,
  input  CLK,
  output [15:0] O
);

  wire oneticklatch_1_out_2;
  wire [15:0] adder_1_out, multiplexer_1_out;

  Adder #(.width(16)) adder_1 (.a(O), .b(16'h1), .out(adder_1_out));  // open: cin, cout
  Register #(.width(16)) register_1 (.D(multiplexer_1_out), .en(EN), .clk(CLK), .Q(O), .clr(oneticklatch_1_out_2));
  Multiplexer #(.width(16)) multiplexer_1 (.in0(adder_1_out), .in1(JMP_ADDR), .out(multiplexer_1_out), .sel(JMP_EN));
  OneTickLatch oneticklatch_1 (.CLK(CLK), .out_2(oneticklatch_1_out_2));
endmodule

module ALU (
  input  [15:0] Input1,
  input  [15:0] Input2,
  input  [3:0] Func,
  output [15:0] out_4
);

  wire [15:0] adder_1_out, and_1_out, divider_1_out, multiplier_1_out, nand_1_out, nor_1_out, or_1_out,
       subtractor_1_out, undriven, undriven_2, xor_1_out;

  Adder #(.width(16)) adder_1 (.a(Input1), .b(Input2), .out(adder_1_out));  // open: cin, cout
  Subtractor #(.width(16)) subtractor_1 (.a(Input1), .b(Input2), .out(subtractor_1_out));  // open: bin, bout
  Multiplier #(.width(16)) multiplier_1 (.a(Input1), .b(Input2), .out(multiplier_1_out));  // open: cin, cout
  Divider #(.width(16)) divider_1 (.a(Input1), .b(Input2), .out(divider_1_out));  // open: upper, rem
  assign and_1_out = Input1 & Input2;  // AND_Gate and_1, 16 bits wide
  assign or_1_out = Input1 | Input2;  // OR_Gate or_1, 16 bits wide
  assign xor_1_out = Input1 ^ Input2;  // XOR_Gate xor_1, 16 bits wide
  assign nand_1_out = ~(Input1 & Input2);  // NAND_Gate nand_1, 16 bits wide
  assign nor_1_out = ~(Input1 | Input2);  // NOR_Gate nor_1, 16 bits wide
  ALU_MUX alu_mux_1 (
    .IN0(adder_1_out), .IN1(subtractor_1_out), .IN2(multiplier_1_out), .IN3(divider_1_out), .IN4(and_1_out),
    .IN5(or_1_out), .IN6(xor_1_out), .IN7(nand_1_out), .IN8(nor_1_out), .IN10(undriven), .IN11(undriven_2),
    .SEL(Func), .MuxOut(out_4));  // open: IN9
endmodule

module ALU_MUX (
  input  [15:0] IN0,
  input  [15:0] IN1,
  input  [15:0] IN2,
  input  [15:0] IN3,
  input  [15:0] IN4,
  input  [15:0] IN5,
  input  [15:0] IN6,
  input  [15:0] IN7,
  input  [15:0] IN8,
  input  [15:0] IN9,
  input  [15:0] IN10,
  input  [15:0] IN11,
  input  [3:0] SEL,
  output [15:0] MuxOut
);

  wire [15:0] multiplexer_1_out, multiplexer_2_out, multiplexer_3_out, multiplexer_4_out, multiplexer_5_out,
       multiplexer_6_out, multiplexer_7_out, multiplexer_8_out, multiplexer_9_out, multiplexer_10_out,
       multiplexer_11_out;

  Multiplexer #(.width(16)) multiplexer_1 (.in0(IN0), .in1(IN1), .out(multiplexer_1_out), .sel(SEL[3]));
  Multiplexer #(.width(16)) multiplexer_2 (.in0(IN2), .in1(IN3), .out(multiplexer_2_out), .sel(SEL[3]));
  Multiplexer #(.width(16)) multiplexer_3 (.in0(IN4), .in1(IN5), .out(multiplexer_3_out), .sel(SEL[3]));
  Multiplexer #(.width(16)) multiplexer_4 (.in0(IN6), .in1(IN7), .out(multiplexer_4_out), .sel(SEL[3]));
  Multiplexer #(.width(16)) multiplexer_5 (.in0(IN8), .in1(IN9), .out(multiplexer_5_out), .sel(SEL[3]));
  Multiplexer #(.width(16)) multiplexer_6 (.in0(IN10), .in1(IN11), .out(multiplexer_6_out), .sel(SEL[3]));
  Multiplexer #(.width(16)) multiplexer_7 (
    .in0(multiplexer_1_out), .in1(multiplexer_2_out), .out(multiplexer_7_out), .sel(SEL[2]));
  Multiplexer #(.width(16)) multiplexer_8 (
    .in0(multiplexer_3_out), .in1(multiplexer_4_out), .out(multiplexer_8_out), .sel(SEL[2]));
  Multiplexer #(.width(16)) multiplexer_9 (
    .in0(multiplexer_5_out), .in1(multiplexer_6_out), .out(multiplexer_9_out), .sel(SEL[2]));
  Multiplexer #(.width(16)) multiplexer_10 (
    .in0(multiplexer_7_out), .in1(multiplexer_8_out), .out(multiplexer_10_out), .sel(SEL[1]));
  Multiplexer #(.width(16)) multiplexer_11 (
    .in1(multiplexer_9_out), .out(multiplexer_11_out), .sel(SEL[1]));  // open: in0
  Multiplexer #(.width(16)) multiplexer_12 (
    .in0(multiplexer_10_out), .in1(multiplexer_11_out), .out(MuxOut), .sel(SEL[0]));
endmodule
